# Fritzing sketch FermenterController (saved by Fritzing 1.0.4)
breadboards: 1

parts:
  Mod1 = Amica NodeMCU DEVKIT 1.0
  F1 = Fan - 4 wire [package=THT]
  LCD1 = LCD1602-I2C
  A2 = 1 chan 3v relay module
  DS1 = DS18B20 1-Wire Temperature Sensor Probe
  J1 = Power Jack [package=power_jack_pth_lock]
  R1 = Resistor [tolerance=±5% resistance=4.7k package=THT]

nets:
  VCC: Mod1.pin1, Mod1.pin_10, Mod1.pin_26, LCD1.VCC, A2.pin_1, DS1.VDD, R1.Pin_1
  GND: Mod1.pin2, Mod1.pin_9, Mod1.pin_25, Mod1.pin_29, LCD1.GND, A2.pin_3, DS1.GND
  N1: Mod1.pin8, A2.pin_2
  N2: Mod1.pin_11, DS1.DQ, R1.Pin_0
  N3: Mod1.pin_13, LCD1.SCL
  N4: Mod1.pin_14, LCD1.SDA
  GND_2: F1.GND, J1.GND
  N5: F1.Power, A2.pin_7
  N6: A2.pin_6, J1.PWR

custom parts:
  Fan - 4 wire: Fan, 4 wire with tach.
  LCD1602-I2C: A standard character display, usually with 2x16 characters. Comes in many colors with LCM1602 IIC attached.
  1 chan 3v relay module: Single 3V relay isolated drive control module High level drive board.
